# Fritzing sketch schematics (saved by Fritzing 0.8.7b)
circuit board: 8.47cm x 5.64444cm
breadboards: 1

parts:
  RFID = Parallax RFID Reader Module
  Flow = IC, SIP package, 3 pins [chip_label=Flowmeter]
  HFD1 = HFD27 [part_number=HFD]
  Valve = SIP - 2 pins [chip_label=Valve package="SIP (Single Inline) [THT]"]
  Coin = IC, SIP package, 4 pins [chip_label="Coin acceptor"]
  D1 = Rectifier Diode [part_number=1N4001 package="300 mil [THT]"]
  Part1 = Arduino Board Ethernet
  12v = SIP - 2 pins [chip_label=12v package="SIP (Single Inline) [THT]"]
  D2 = Rectifier Diode [part_number=1N4001 package="300 mil [THT]"]
  Nokia_LCD = Adafruit Nokia 5510
  Nokia_LCD_2 = Adafruit Nokia 5510
  Nokia_LCD_3 = Adafruit Nokia 5510
  U2 = Voltage Regulator - 5V [package="TO220 [THT]"]

nets:
  VCC: RFID.VCC, Part1.5V, Nokia_LCD.Vcc, Nokia_LCD.LED, Nokia_LCD_2.Vcc, Nokia_LCD_2.LED, Nokia_LCD_3.Vcc, Nokia_LCD_3.LED, U2.output_voltage
  N1: RFID./ENABLE, Part1.D9_PWM
  N2: RFID.Sout, Part1.D0/RX
  GND: RFID.GND, Flow.pin3, HFD1.pin1, Valve.pin2, Coin.pin2, D1.anode, Part1.GND, 12v.pin2, D2.anode, Nokia_LCD.GND, Nokia_LCD_2.GND, Nokia_LCD_3.GND, U2.GND
  N3: Flow.pin1, HFD1.pin13, Coin.pin1, Part1.VIN, 12v.pin1, U2.input_voltage
  N4: Flow.pin2, Part1.D2_PWM
  N5: HFD1.pin9, Valve.pin1, D1.cathode
  N6: HFD1.pin16, Part1.A1, D2.cathode
  N7: Coin.pin3, Part1.D3_PWM
  N8: Coin.pin4, Part1.A2
  N9: Part1.D8, Nokia_LCD.CLK, Nokia_LCD_2.CLK, Nokia_LCD_3.CLK
  N10: Part1.D4, Nokia_LCD.RST, Nokia_LCD_2.RST, Nokia_LCD_3.RST
  N11: Part1.D5_PWM, Nokia_LCD.CS, Nokia_LCD_2.CS, Nokia_LCD_3.CS
  N12: Part1.D6_PWM, Nokia_LCD.D/C, Nokia_LCD_2.D/C, Nokia_LCD_3.D/C
  N13: Part1.D7, Nokia_LCD.DIN, Nokia_LCD_2.DIN, Nokia_LCD_3.DIN

notes:
  RFID
  LCD
  Flow
  HFD
  Valve
  Coin
  12v
  D1
  VCC
  GND
  LED
  SCLK
  DC
  CS
  RST
  DIN
  Enable
  Data
  vcc
  D2
  v1.0
  Vreg
  out
  2014

custom parts:
  HFD27: HFD27 Relay
  : Nokia 5110 LCD with 8 pin. It's a 45mm*45mm module part. Description: The Nokia 5110 is a basic graphic LCD screen for lots of applications. It was originally intended for as a cell phone screen. This one is mounted on an easy to solder PCB. It uses the PCD8544 controller. The PCD8544 is a low power CMOS LCD controller/driver, designed to drive a graphic display of 48 rows and 84 columns. All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
